// Logisim project Lab05.circ as structural Verilog: 8 circuits, main circuit main
module main (
  input  Reset,
  input  [2:0] Selector,
  output [3:0] Probe1
);

  Clock sysclk ();  // open: out
  Universal universal_1 (.Reset(Reset), .Selector(Selector), .Universal_output(Probe1));
  Hex_Digit_Display hex_digit_display_1 (.value(Probe1));  // open: dp
endmodule

module D_flip_flop_up_counter (
  input  clk,
  input  R,
  output [3:0] Up
);

  wire d_ff_1_qn, d_ff_2_qn, d_ff_3_qn, d_ff_4_qn;

  D_Flip_Flop d_ff_1 (.D(d_ff_1_qn), .clk(clk), .Q(Up[0]), .Qn(d_ff_1_qn), .reset(R));  // open: preset
  D_Flip_Flop d_ff_2 (.D(d_ff_2_qn), .clk(d_ff_1_qn), .Q(Up[1]), .Qn(d_ff_2_qn), .reset(R));  // open: preset
  D_Flip_Flop d_ff_3 (.D(d_ff_3_qn), .clk(d_ff_2_qn), .Q(Up[2]), .Qn(d_ff_3_qn), .reset(R));  // open: preset
  D_Flip_Flop d_ff_4 (.D(d_ff_4_qn), .clk(d_ff_3_qn), .Q(Up[3]), .Qn(d_ff_4_qn), .reset(R));  // open: preset
endmodule

module D_flip_flop_down_counter (
  input  clk,
  input  R,
  output [3:0] Down
);

  wire d_ff_1_qn, d_ff_2_qn, d_ff_3_qn, d_ff_4_qn;

  D_Flip_Flop d_ff_1 (.D(d_ff_1_qn), .clk(clk), .Q(Down[0]), .Qn(d_ff_1_qn), .preset(R));  // open: reset
  D_Flip_Flop d_ff_2 (.D(d_ff_2_qn), .clk(Down[0]), .Q(Down[1]), .Qn(d_ff_2_qn), .preset(R));  // open: reset
  D_Flip_Flop d_ff_3 (.D(d_ff_3_qn), .clk(Down[1]), .Q(Down[2]), .Qn(d_ff_3_qn), .preset(R));  // open: reset
  D_Flip_Flop d_ff_4 (.D(d_ff_4_qn), .clk(Down[2]), .Q(Down[3]), .Qn(d_ff_4_qn), .preset(R));  // open: reset
endmodule

module D_flip_flop (
  input  D,
  input  clk,
  output Q,
  output not_Q
);

  wire nand_1_out, nand_2_out, not_1_out;

  not not_1 (not_1_out, D);
  nand nand_1 (nand_1_out, D, clk);
  nand nand_2 (nand_2_out, clk, not_1_out);
  nand nand_3 (Q, nand_1_out, not_Q);
  nand nand_4 (not_Q, Q, nand_2_out);
endmodule

module decade_counter (
  input  clk,
  input  R,
  output [3:0] Decade
);

  wire and_1_out, d_ff_1_qn, d_ff_2_qn, d_ff_3_qn, d_ff_4_qn, or_1_out;

  D_Flip_Flop d_ff_1 (.D(d_ff_1_qn), .clk(clk), .Q(Decade[0]), .Qn(d_ff_1_qn), .reset(or_1_out));  // open: preset
  or or_1 (or_1_out, R, and_1_out);
  D_Flip_Flop d_ff_2 (.D(d_ff_2_qn), .clk(d_ff_1_qn), .Q(Decade[1]), .Qn(d_ff_2_qn), .reset(or_1_out));  // open: preset
  D_Flip_Flop d_ff_3 (.D(d_ff_3_qn), .clk(d_ff_2_qn), .Q(Decade[2]), .Qn(d_ff_3_qn), .reset(or_1_out));  // open: preset
  D_Flip_Flop d_ff_4 (.D(d_ff_4_qn), .clk(d_ff_3_qn), .Q(Decade[3]), .Qn(d_ff_4_qn), .reset(or_1_out));  // open: preset
  and and_1 (and_1_out, Decade[1], Decade[3]);
endmodule

module ring_counter (
  input  clk,
  input  R,
  output [3:0] RIng
);

  D_Flip_Flop d_ff_1 (.D(RIng[3]), .clk(clk), .Q(RIng[0]), .preset(R));  // open: Qn, reset
  D_Flip_Flop d_ff_2 (.D(RIng[0]), .clk(clk), .Q(RIng[1]), .reset(R));  // open: Qn, preset
  D_Flip_Flop d_ff_3 (.D(RIng[1]), .clk(clk), .Q(RIng[2]), .reset(R));  // open: Qn, preset
  D_Flip_Flop d_ff_4 (.D(RIng[2]), .clk(clk), .Q(RIng[3]), .reset(R));  // open: Qn, preset
endmodule

module johnson_counter (
  input  clk,
  input  R,
  output [3:0] Johnson
);

  wire d_ff_4_qn;

  D_Flip_Flop d_ff_1 (.D(d_ff_4_qn), .clk(clk), .Q(Johnson[0]), .preset(R));  // open: Qn, reset
  D_Flip_Flop d_ff_2 (.D(Johnson[0]), .clk(clk), .Q(Johnson[1]), .reset(R));  // open: Qn, preset
  D_Flip_Flop d_ff_3 (.D(Johnson[1]), .clk(clk), .Q(Johnson[2]), .reset(R));  // open: Qn, preset
  D_Flip_Flop d_ff_4 (.D(Johnson[2]), .clk(clk), .Q(Johnson[3]), .Qn(d_ff_4_qn), .reset(R));  // open: preset
endmodule

module Universal (
  input  Reset,
  input  [2:0] Selector,
  output [3:0] Universal_output
);

  wire clk_out;
  wire [3:0] d_flip_flop_down_counter_1_down, d_flip_flop_up_counter_1_up, decade_counter_1_decade,
       johnson_counter_1_johnson, ring_counter_1_ring;

  Clock clk (.out(clk_out));
  D_flip_flop_up_counter d_flip_flop_up_counter_1 (.clk(clk_out), .R(Reset), .Up(d_flip_flop_up_counter_1_up));
  D_flip_flop_down_counter d_flip_flop_down_counter_1 (
    .clk(clk_out), .R(Reset), .Down(d_flip_flop_down_counter_1_down));
  decade_counter decade_counter_1 (.clk(clk_out), .R(Reset), .Decade(decade_counter_1_decade));
  ring_counter ring_counter_1 (.clk(clk_out), .R(Reset), .RIng(ring_counter_1_ring));
  johnson_counter johnson_counter_1 (.clk(clk_out), .R(Reset), .Johnson(johnson_counter_1_johnson));
  Multiplexer #(.select(3), .width(4)) multiplexer_1 (
    .in0(d_flip_flop_up_counter_1_up), .in1(d_flip_flop_down_counter_1_down), .in2(decade_counter_1_decade),
    .in3(ring_counter_1_ring), .in4(johnson_counter_1_johnson), .in5(4'b0000), .in6(4'b0000), .in7(4'b0000),
    .out(Universal_output), .sel(Selector));
endmodule
